// Logisim project game.circ as structural Verilog: 4 circuits, main circuit main
module main (
);

  wire ACERTADO_0000, ACERTADO_0001, ACERTADO_0010, ACERTADO_0011, ACERTADO_0100, ACERTADO_0101,
       ACERTADO_0110, ACERTADO_0111, ACERTADO_1000, ACERTADO_1001, ACERTADO_1010, ACERTADO_1011,
       ACERTADO_1100, ACERTADO_1101, ACERTADO_1110, ACERTADO_1111, and_1_out, and_2_out, and_3_out,
       and_4_out, and_5_out, and_6_out, and_7_out, and_8_out, and_13_out, and_14_out, and_15_out, and_16_out,
       and_17_out, and_18_out, and_19_out, and_20_out, and_25_out, and_26_out, and_27_out, and_28_out,
       and_29_out, and_30_out, and_31_out, and_32_out, and_33_out, and_50_out, and_51_out, and_52_out,
       and_53_out, and_54_out, and_55_out, and_56_out, and_57_out, and_58_out, and_67_out, and_72_out,
       and_73_out, and_74_out, and_75_out, and_76_out, and_77_out, and_78_out, and_79_out, and_80_out,
       and_81_out, and_82_out, and_83_out, and_84_out, and_85_out, and_86_out, and_87_out, and_88_out,
       and_89_out, and_90_out, and_91_out, and_92_out, and_93_out, and_94_out, and_95_out, and_97_out,
       and_98_out, and_99_out, and_100_out, and_101_out, and_102_out, and_103_out, and_104_out, and_105_out,
       and_106_out, and_107_out, and_108_out, and_109_out, and_110_out, and_111_out, and_112_out,
       and_113_out, and_114_out, and_115_out, and_116_out, and_117_out, and_118_out, and_119_out,
       and_120_out, Botao_coluna, Botao_linha, Check, comparator_1_eq, comparator_2_eq, Confirma,
       counter_19_q, escolher_1_s1, escolher_1_s2, Estado_0, Estado_1, Estado_2, Estado_3, iguais_1_s, L0000,
       L0001, L0010, L0011, L0100, L0101, L0110, L0111, L1000, L1001, L1010, L1011, L1100, L1101, L1110,
       L1111, MUX_0000, MUX_0001, MUX_0010, MUX_0011, MUX_0100, MUX_0101, MUX_0110, MUX_0111, MUX_1000,
       MUX_1001, MUX_1010, MUX_1011, MUX_1100, MUX_1101, MUX_1110, MUX_1111, NAO_ACERTADO, or_1_out,
       or_2_out, or_3_out, or_4_out, or_5_out, or_6_out, or_7_out, or_8_out, or_9_out, or_10_out, or_11_out,
       or_12_out, or_13_out, or_14_out, or_15_out, or_16_out, or_17_out, Reset, saida0000, saida0001,
       saida0010, saida0011, saida0100, saida0101, saida0110, saida0111, saida1000, saida1001, saida1010,
       saida1011, saida1100, saida1101, saida1110, saida1111;
  wire [1:0] Coluna, Coluna_1, Coluna_2, counter_2_q, Linha, Linha_1, Linha_2;
  wire [3:0] counter_14_q, Jogador_1, Jogador_2, multiplexer_5_out, multiplexer_10_out, V0000, V0001, V0010,
       V0011, V0100, V0101, V0110, V0111, V1000, V1001, V1010, V1011, V1100, V1101, V1110, V1111, Vez_jogador;

  and and_1 (and_1_out, ~Coluna_1[0], ~Coluna_1[1], ~Linha_1[0], ~Linha_1[1]);  // AND_Gate
  and and_2 (and_2_out, ~Coluna_2[0], ~Coluna_2[1], ~Linha_2[0], ~Linha_2[1]);  // AND_Gate
  and and_3 (and_3_out, Coluna_1[0], ~Coluna_1[1], ~Linha_1[0], ~Linha_1[1]);  // AND_Gate
  and and_4 (and_4_out, Coluna_2[0], ~Coluna_2[1], ~Linha_2[0], ~Linha_2[1]);  // AND_Gate
  and and_5 (and_5_out, ~Coluna_1[0], Coluna_1[1], ~Linha_1[0], ~Linha_1[1]);  // AND_Gate
  and and_6 (and_6_out, ~Coluna_2[0], Coluna_2[1], ~Linha_2[0], ~Linha_2[1]);  // AND_Gate
  and and_7 (and_7_out, Coluna_1[0], Coluna_1[1], ~Linha_1[0], ~Linha_1[1]);  // AND_Gate
  and and_8 (and_8_out, Coluna_2[0], Coluna_2[1], ~Linha_2[0], ~Linha_2[1]);  // AND_Gate
  Button button_1 (.out(Botao_linha));
  Button button_2 (.out(Confirma));
  or or_1 (or_1_out, and_1_out, and_2_out);
  or or_2 (or_2_out, and_3_out, and_4_out);
  or or_3 (or_3_out, and_5_out, and_6_out);
  or or_4 (or_4_out, and_7_out, and_8_out);
  LED led_1 (.in(L0000));
  Hex_Digit_Display hex_digit_display_1 (.value(V0000));  // open: dp
  LED led_2 (.in(L0100));
  Hex_Digit_Display hex_digit_display_2 (.value(V0100));  // open: dp
  LED led_3 (.in(L1000));
  Hex_Digit_Display hex_digit_display_3 (.value(V1000));  // open: dp
  LED led_4 (.in(L1100));
  Hex_Digit_Display hex_digit_display_4 (.value(V1100));  // open: dp
  and and_9 (ACERTADO_0000, Check, or_1_out);
  and and_10 (ACERTADO_0001, Check, or_2_out);
  and and_11 (ACERTADO_0010, Check, or_3_out);
  and and_12 (ACERTADO_0011, Check, or_4_out);
  Button button_3 (.out(Botao_coluna));
  Button button_4 (.out(Reset));
  LED led_5 (.in(L0001));
  Hex_Digit_Display hex_digit_display_5 (.value(V0001));  // open: dp
  LED led_6 (.in(L0101));
  Hex_Digit_Display hex_digit_display_6 (.value(V0101));  // open: dp
  LED led_7 (.in(L1001));
  Hex_Digit_Display hex_digit_display_7 (.value(V1001));  // open: dp
  LED led_8 (.in(L1101));
  Hex_Digit_Display hex_digit_display_8 (.value(V1101));  // open: dp
  Hex_Digit_Display hex_digit_display_9 (.value(Vez_jogador));  // open: dp
  LED led_9 (.in(L0010));
  Hex_Digit_Display hex_digit_display_10 (.value(V0010));  // open: dp
  LED led_10 (.in(L0110));
  Hex_Digit_Display hex_digit_display_11 (.value(V0110));  // open: dp
  LED led_11 (.in(L1010));
  Hex_Digit_Display hex_digit_display_12 (.value(V1010));  // open: dp
  LED led_12 (.in(L1110));
  Hex_Digit_Display hex_digit_display_13 (.value(V1110));  // open: dp
  Hex_Digit_Display hex_digit_display_14 (.value(Jogador_1));  // open: dp
  LED led_13 (.in(L0011));
  Hex_Digit_Display hex_digit_display_15 (.value(V0011));  // open: dp
  LED led_14 (.in(L0111));
  Hex_Digit_Display hex_digit_display_16 (.value(V0111));  // open: dp
  LED led_15 (.in(L1011));
  Hex_Digit_Display hex_digit_display_17 (.value(V1011));  // open: dp
  LED led_16 (.in(L1111));
  Hex_Digit_Display hex_digit_display_18 (.value(V1111));  // open: dp
  and and_13 (and_13_out, ~Coluna_1[0], ~Coluna_1[1], Linha_1[0], ~Linha_1[1]);  // AND_Gate
  and and_14 (and_14_out, ~Coluna_2[0], ~Coluna_2[1], Linha_2[0], ~Linha_2[1]);  // AND_Gate
  and and_15 (and_15_out, Coluna_1[0], ~Coluna_1[1], Linha_1[0], ~Linha_1[1]);  // AND_Gate
  and and_16 (and_16_out, Coluna_2[0], ~Coluna_2[1], Linha_2[0], ~Linha_2[1]);  // AND_Gate
  and and_17 (and_17_out, ~Coluna_1[0], Coluna_1[1], Linha_1[0], ~Linha_1[1]);  // AND_Gate
  and and_18 (and_18_out, ~Coluna_2[0], Coluna_2[1], Linha_2[0], ~Linha_2[1]);  // AND_Gate
  and and_19 (and_19_out, Coluna_1[0], Coluna_1[1], Linha_1[0], ~Linha_1[1]);  // AND_Gate
  and and_20 (and_20_out, Coluna_2[0], Coluna_2[1], Linha_2[0], ~Linha_2[1]);  // AND_Gate
  Hex_Digit_Display hex_digit_display_19 (.value(Jogador_2));  // open: dp
  or or_5 (or_5_out, and_13_out, and_14_out);
  or or_6 (or_6_out, and_15_out, and_16_out);
  or or_7 (or_7_out, and_17_out, and_18_out);
  or or_8 (or_8_out, and_19_out, and_20_out);
  and and_21 (ACERTADO_0100, Check, or_5_out);
  and and_22 (ACERTADO_0101, Check, or_6_out);
  and and_23 (ACERTADO_0110, Check, or_7_out);
  and and_24 (ACERTADO_0111, Check, or_8_out);
  and and_25 (and_25_out, ~Coluna_1[0], ~Coluna_1[1], ~Linha_1[0], Linha_1[1]);  // AND_Gate
  and and_26 (and_26_out, ~Coluna_2[0], ~Coluna_2[1], ~Linha_2[0], Linha_2[1]);  // AND_Gate
  and and_27 (and_27_out, Coluna_1[0], ~Coluna_1[1], ~Linha_1[0], Linha_1[1]);  // AND_Gate
  and and_28 (and_28_out, Coluna_2[0], ~Coluna_2[1], ~Linha_2[0], Linha_2[1]);  // AND_Gate
  and and_29 (and_29_out, ~Coluna_1[0], Coluna_1[1], ~Linha_1[0], Linha_1[1]);  // AND_Gate
  and and_30 (and_30_out, ~Coluna_2[0], Coluna_2[1], ~Linha_2[0], Linha_2[1]);  // AND_Gate
  and and_31 (and_31_out, Coluna_1[0], Coluna_1[1], ~Linha_1[0], Linha_1[1]);  // AND_Gate
  and and_32 (and_32_out, Coluna_2[0], Coluna_2[1], ~Linha_2[0], Linha_2[1]);  // AND_Gate
  or or_9 (or_9_out, and_25_out, and_26_out);
  or or_10 (or_10_out, and_27_out, and_28_out);
  or or_11 (or_11_out, and_29_out, and_30_out);
  or or_12 (or_12_out, and_31_out, and_32_out);
  Counter #(.width(2), .max('h3)) counter_1 (.Q(Linha), .clk(Botao_linha), .clr(Reset));  // open: load, D, count, carry
  and and_33 (and_33_out, NAO_ACERTADO, iguais_1_s);
  Comparator #(.width(4)) comparator_1 (
    .a({Coluna_1, Linha_1}), .b({Coluna, Linha}), .eq(comparator_1_eq));  // open: gt, lt
  and and_34 (ACERTADO_1000, Check, or_9_out);
  and and_35 (ACERTADO_1001, Check, or_10_out);
  and and_36 (ACERTADO_1010, Check, or_11_out);
  and and_37 (ACERTADO_1011, Check, or_12_out);
  and and_38 (L0000, ~Linha[1], ~Linha[0], ~Coluna[1], ~Coluna[0]);  // AND_Gate
  and and_39 (L0100, ~Linha[1], Linha[0], ~Coluna[1], ~Coluna[0]);  // AND_Gate
  and and_40 (L1000, Linha[1], ~Linha[0], ~Coluna[1], ~Coluna[0]);  // AND_Gate
  and and_41 (L1100, Linha[1], Linha[0], ~Coluna[1], ~Coluna[0]);  // AND_Gate
  Counter #(.width(2), .max('h3), .trigger("falling")) counter_2 (
    .Q(counter_2_q), .clk(and_33_out), .clr(or_13_out));  // open: load, D, count, carry
  iguais iguais_1 (.conf(Confirma), .comp(comparator_1_eq), .est1(Estado_1), .s(iguais_1_s));
  or or_13 (or_13_out, Reset, Estado_3);
  Counter #(.width(2), .max('h3)) counter_3 (
    .Q(Coluna), .clk(Botao_coluna), .clr(Reset));  // open: load, D, count, carry
  and and_42 (Estado_0, ~counter_2_q[0], ~counter_2_q[1]);  // AND_Gate
  and and_43 (Estado_1, counter_2_q[0], ~counter_2_q[1]);  // AND_Gate
  and and_44 (Estado_2, ~counter_2_q[0], counter_2_q[1]);  // AND_Gate
  and and_45 (Estado_3, counter_2_q[0], counter_2_q[1]);
  and and_46 (L0001, ~Linha[1], ~Linha[0], ~Coluna[1], Coluna[0]);  // AND_Gate
  and and_47 (L0101, ~Linha[1], Linha[0], ~Coluna[1], Coluna[0]);  // AND_Gate
  and and_48 (L1001, Linha[1], ~Linha[0], ~Coluna[1], Coluna[0]);  // AND_Gate
  and and_49 (L1101, Linha[1], Linha[0], ~Coluna[1], Coluna[0]);  // AND_Gate
  and and_50 (and_50_out, ~Coluna_1[0], ~Coluna_1[1], Linha_1[0], Linha_1[1]);  // AND_Gate
  and and_51 (and_51_out, ~Coluna_2[0], ~Coluna_2[1], Linha_2[0], Linha_2[1]);  // AND_Gate
  and and_52 (and_52_out, Coluna_1[0], ~Coluna_1[1], Linha_1[0], Linha_1[1]);  // AND_Gate
  and and_53 (and_53_out, Coluna_2[0], ~Coluna_2[1], Linha_2[0], Linha_2[1]);  // AND_Gate
  and and_54 (and_54_out, ~Coluna_1[0], Coluna_1[1], Linha_1[0], Linha_1[1]);  // AND_Gate
  and and_55 (and_55_out, ~Coluna_2[0], Coluna_2[1], Linha_2[0], Linha_2[1]);  // AND_Gate
  and and_56 (and_56_out, Coluna_1[0], Coluna_1[1], Linha_1[0], Linha_1[1]);
  and and_57 (and_57_out, Coluna_2[0], Coluna_2[1], Linha_2[0], Linha_2[1]);
  and and_58 (and_58_out, Confirma, Estado_0);
  or or_14 (or_14_out, and_50_out, and_51_out);
  or or_15 (or_15_out, and_52_out, and_53_out);
  or or_16 (or_16_out, and_54_out, and_55_out);
  or or_17 (or_17_out, and_56_out, and_57_out);
  Register #(.width(2)) register_1 (.D(Linha), .Q(Linha_1), .clk(and_58_out), .clr(Reset));  // open: en
  Register #(.width(2)) register_2 (.D(Coluna), .Q(Coluna_1), .clk(and_58_out), .clr(Reset));  // open: en
  and and_59 (ACERTADO_1100, Check, or_14_out);
  and and_60 (ACERTADO_1101, Check, or_15_out);
  and and_61 (ACERTADO_1110, Check, or_16_out);
  and and_62 (ACERTADO_1111, Check, or_17_out);
  and and_63 (L0010, ~Linha[1], ~Linha[0], Coluna[1], ~Coluna[0]);  // AND_Gate
  and and_64 (L0110, ~Linha[1], Linha[0], Coluna[1], ~Coluna[0]);  // AND_Gate
  and and_65 (L1010, Linha[1], ~Linha[0], Coluna[1], ~Coluna[0]);  // AND_Gate
  and and_66 (L1110, Linha[1], Linha[0], Coluna[1], ~Coluna[0]);  // AND_Gate
  Register #(.width(2)) register_3 (.D(Linha), .Q(Linha_2), .clk(and_67_out), .clr(Reset));  // open: en
  Register #(.width(2)) register_4 (.D(Coluna), .Q(Coluna_2), .clk(and_67_out), .clr(Reset));  // open: en
  and and_67 (and_67_out, Confirma, Estado_1);
  and and_68 (L0011, ~Linha[1], ~Linha[0], Coluna[1], Coluna[0]);  // AND_Gate
  and and_69 (L0111, ~Linha[1], Linha[0], Coluna[1], Coluna[0]);  // AND_Gate
  and and_70 (L1011, Linha[1], ~Linha[0], Coluna[1], Coluna[0]);  // AND_Gate
  and and_71 (L1111, Linha[1], Linha[0], Coluna[1], Coluna[0]);
  and and_72 (and_72_out, Estado_2, ~Coluna_2[0], ~Coluna_2[1], ~Linha_2[0], ~Linha_2[1]);  // AND_Gate
  and and_73 (and_73_out, ~Estado_0, ~Coluna_1[0], ~Coluna_1[1], ~Linha_1[0], ~Linha_1[1]);  // AND_Gate
  Counter #(.width(1), .max('h1)) counter_4 (
    .Q(saida0000), .clk(ACERTADO_0000), .clr(Reset));  // open: load, D, count, carry
  and and_74 (and_74_out, Estado_2, ~Coluna_2[0], ~Coluna_2[1], Linha_2[0], ~Linha_2[1]);  // AND_Gate
  and and_75 (and_75_out, ~Estado_0, ~Coluna_1[0], ~Coluna_1[1], Linha_1[0], ~Linha_1[1]);  // AND_Gate
  Counter #(.width(1), .max('h1)) counter_5 (
    .Q(saida0100), .clk(ACERTADO_0100), .clr(Reset));  // open: load, D, count, carry
  and and_76 (and_76_out, Estado_2, ~Coluna_2[0], ~Coluna_2[1], ~Linha_2[0], Linha_2[1]);  // AND_Gate
  and and_77 (and_77_out, ~Estado_0, ~Coluna_1[0], ~Coluna_1[1], ~Linha_1[0], Linha_1[1]);  // AND_Gate
  Counter #(.width(1), .max('h1)) counter_6 (
    .Q(saida1000), .clk(ACERTADO_1000), .clr(Reset));  // open: load, D, count, carry
  and and_78 (and_78_out, Estado_2, ~Coluna_2[0], ~Coluna_2[1], Linha_2[0], Linha_2[1]);  // AND_Gate
  and and_79 (and_79_out, ~Estado_0, ~Coluna_1[0], ~Coluna_1[1], Linha_1[0], Linha_1[1]);  // AND_Gate
  Counter #(.width(1), .max('h1)) counter_7 (
    .Q(saida1100), .clk(ACERTADO_1100), .clr(Reset));  // open: load, D, count, carry
  or or_18 (MUX_0000, and_72_out, and_73_out, saida0000);
  or or_19 (MUX_0100, and_74_out, and_75_out, saida0100);
  or or_20 (MUX_1000, and_76_out, and_77_out, saida1000);
  or or_21 (MUX_1100, and_78_out, and_79_out, saida1100);
  and and_80 (and_80_out, Estado_2, Coluna_2[0], ~Coluna_2[1], ~Linha_2[0], ~Linha_2[1]);  // AND_Gate
  and and_81 (and_81_out, ~Estado_0, Coluna_1[0], ~Coluna_1[1], ~Linha_1[0], ~Linha_1[1]);  // AND_Gate
  Counter #(.width(1), .max('h1)) counter_8 (
    .Q(saida0001), .clk(ACERTADO_0001), .clr(Reset));  // open: load, D, count, carry
  and and_82 (and_82_out, ~Estado_0, Coluna_1[0], ~Coluna_1[1], Linha_1[0], ~Linha_1[1]);  // AND_Gate
  Counter #(.width(1), .max('h1)) counter_9 (
    .Q(saida0101), .clk(ACERTADO_0101), .clr(Reset));  // open: load, D, count, carry
  Counter #(.width(1), .max('h1)) counter_10 (
    .Q(saida1001), .clk(ACERTADO_1001), .clr(Reset));  // open: load, D, count, carry
  Counter #(.width(1), .max('h1)) counter_11 (
    .Q(saida1101), .clk(ACERTADO_1101), .clr(Reset));  // open: load, D, count, carry
  Multiplexer #(.width(4)) multiplexer_1 (.in1(4'b1111), .out(V0000), .sel(MUX_0000));  // open: in0, en
  Multiplexer #(.width(4)) multiplexer_2 (.in1(4'b0010), .out(V0100), .sel(MUX_0100));  // open: in0, en
  Multiplexer #(.width(4)) multiplexer_3 (.in1(4'b1100), .out(V1000), .sel(MUX_1000));  // open: in0, en
  Multiplexer #(.width(4)) multiplexer_4 (.in1(4'b1110), .out(V1100), .sel(MUX_1100));  // open: in0, en
  Multiplexer #(.select(4), .width(4)) multiplexer_5 (
    .in0(4'b1111), .in1(4'b1111), .in2(4'b1010), .in3(4'b1010), .in4(4'b0010), .in5(4'b0010), .in6(4'b1011),
    .in7(4'b1011), .in8(4'b1100), .in9(4'b1100), .in10(4'b1101), .in11(4'b1101), .in12(4'b1110),
    .in13(4'b1110), .in14(4'b0111), .in15(4'b0111), .out(multiplexer_5_out), .sel({Linha_1, Coluna_1}));  // open: en
  or or_22 (MUX_0001, and_80_out, and_81_out, saida0001);
  and and_83 (and_83_out, Estado_2, Coluna_2[0], ~Coluna_2[1], Linha_2[0], ~Linha_2[1]);  // AND_Gate
  or or_23 (MUX_0101, and_83_out, and_82_out, saida0101);
  and and_84 (and_84_out, Estado_2, Coluna_2[0], ~Coluna_2[1], ~Linha_2[0], Linha_2[1]);  // AND_Gate
  and and_85 (and_85_out, ~Estado_0, Coluna_1[0], ~Coluna_1[1], ~Linha_1[0], Linha_1[1]);  // AND_Gate
  and and_86 (and_86_out, Estado_2, Coluna_2[0], ~Coluna_2[1], Linha_2[0], Linha_2[1]);  // AND_Gate
  and and_87 (and_87_out, ~Estado_0, Coluna_1[0], ~Coluna_1[1], Linha_1[0], Linha_1[1]);  // AND_Gate
  or or_24 (MUX_1001, and_84_out, and_85_out, saida1001);
  or or_25 (MUX_1101, and_86_out, and_87_out, saida1101);
  Multiplexer #(.width(4)) multiplexer_6 (.in1(4'b1111), .out(V0001), .sel(MUX_0001));  // open: in0, en
  Multiplexer #(.width(4)) multiplexer_7 (.in1(4'b0010), .out(V0101), .sel(MUX_0101));  // open: in0, en
  Multiplexer #(.width(4)) multiplexer_8 (.in1(4'b1100), .out(V1001), .sel(MUX_1001));  // open: in0, en
  Multiplexer #(.width(4)) multiplexer_9 (.in1(4'b1110), .out(V1101), .sel(MUX_1101));  // open: in0, en
  Counter #(.width(1), .max('h1)) counter_12 (
    .Q(saida0010), .clk(ACERTADO_0010), .clr(Reset));  // open: load, D, count, carry
  Counter #(.width(1), .max('h1)) counter_13 (
    .Q(saida0110), .clk(ACERTADO_0110), .clr(Reset));  // open: load, D, count, carry
  Multiplexer #(.select(4), .width(4)) multiplexer_10 (
    .in0(4'b1111), .in1(4'b1111), .in2(4'b1010), .in3(4'b1010), .in4(4'b0010), .in5(4'b0010), .in6(4'b1011),
    .in7(4'b1011), .in8(4'b1100), .in9(4'b1100), .in10(4'b1101), .in11(4'b1101), .in12(4'b1110),
    .in13(4'b1110), .in14(4'b0111), .in15(4'b0111), .out(multiplexer_10_out), .sel({Linha_2, Coluna_2}));  // open: en
  Counter #(.width(4), .max('h1)) counter_14 (
    .Q(counter_14_q), .clk(Estado_3), .clr(Reset));  // open: load, D, count, carry
  and and_88 (and_88_out, Estado_2, ~Coluna_2[0], Coluna_2[1], ~Linha_2[0], ~Linha_2[1]);  // AND_Gate
  and and_89 (and_89_out, ~Estado_0, ~Coluna_1[0], Coluna_1[1], ~Linha_1[0], ~Linha_1[1]);  // AND_Gate
  and and_90 (and_90_out, Estado_2, ~Coluna_2[0], Coluna_2[1], Linha_2[0], ~Linha_2[1]);  // AND_Gate
  and and_91 (and_91_out, ~Estado_0, ~Coluna_1[0], Coluna_1[1], Linha_1[0], ~Linha_1[1]);  // AND_Gate
  and and_92 (and_92_out, Estado_2, ~Coluna_2[0], Coluna_2[1], ~Linha_2[0], Linha_2[1]);  // AND_Gate
  and and_93 (and_93_out, ~Estado_0, ~Coluna_1[0], Coluna_1[1], ~Linha_1[0], Linha_1[1]);  // AND_Gate
  Counter #(.width(1), .max('h1)) counter_15 (
    .Q(saida1010), .clk(ACERTADO_1010), .clr(Reset));  // open: load, D, count, carry
  and and_94 (and_94_out, Estado_2, ~Coluna_2[0], Coluna_2[1], Linha_2[0], Linha_2[1]);  // AND_Gate
  and and_95 (and_95_out, ~Estado_0, ~Coluna_1[0], Coluna_1[1], Linha_1[0], Linha_1[1]);  // AND_Gate
  Counter #(.width(1), .max('h1)) counter_16 (
    .Q(saida1110), .clk(ACERTADO_1110), .clr(Reset));  // open: load, D, count, carry
  Multiplexer #(.width(4)) multiplexer_11 (.in1(4'b1010), .out(V0010), .sel(MUX_0010));  // open: in0, en
  Multiplexer #(.width(4)) multiplexer_12 (.in1(4'b1011), .out(V0110), .sel(MUX_0110));  // open: in0, en
  Multiplexer #(.width(4)) multiplexer_13 (.in1(4'b1101), .out(V1010), .sel(MUX_1010));  // open: in0, en
  Multiplexer #(.width(4)) multiplexer_14 (.in1(4'b0111), .out(V1110), .sel(MUX_1110));  // open: in0, en
  Comparator #(.width(4)) comparator_2 (
    .a(multiplexer_5_out), .b(multiplexer_10_out), .eq(comparator_2_eq));  // open: gt, lt
  or or_26 (MUX_0010, and_88_out, and_89_out, saida0010);
  or or_27 (MUX_0110, and_90_out, and_91_out, saida0110);
  or or_28 (MUX_1010, and_92_out, and_93_out, saida1010);
  or or_29 (MUX_1110, and_94_out, and_95_out, saida1110);
  jogador_da_vez jogador_da_vez_1 (
    .a(counter_14_q[3]), .b(counter_14_q[2]), .c(counter_14_q[1]), .d(counter_14_q[0]), .x1(Vez_jogador[3]),
    .x2(Vez_jogador[2]), .x3(Vez_jogador[1]), .x4(Vez_jogador[0]));
  Counter #(.width(4), .max('hf)) counter_17 (
    .Q(Jogador_1), .clk(escolher_1_s2), .clr(Reset));  // open: load, D, count, carry
  and and_96 (Check, comparator_2_eq, Estado_3);
  Multiplexer #(.width(4)) multiplexer_15 (.in1(4'b1010), .out(V0011), .sel(MUX_0011));  // open: in0, en
  Multiplexer #(.width(4)) multiplexer_16 (.in1(4'b1011), .out(V0111), .sel(MUX_0111));  // open: in0, en
  Multiplexer #(.width(4)) multiplexer_17 (.in1(4'b1101), .out(V1011), .sel(MUX_1011));  // open: in0, en
  Multiplexer #(.width(4)) multiplexer_18 (.in1(4'b0111), .out(V1111), .sel(MUX_1111));  // open: in0, en
  Counter #(.width(4), .max('hf)) counter_18 (
    .Q(Jogador_2), .clk(escolher_1_s1), .clr(Reset));  // open: load, D, count, carry
  escolher escolher_1 (.a(counter_19_q), .b(Check), .s1(escolher_1_s1), .s2(escolher_1_s2));
  Counter #(.width(1), .max('h1)) counter_19 (
    .Q(counter_19_q), .clk(Estado_2), .clr(Reset));  // open: load, D, count, carry
  and and_97 (and_97_out, Estado_2, Coluna_2[0], Coluna_2[1], ~Linha_2[0], ~Linha_2[1]);  // AND_Gate
  and and_98 (and_98_out, ~Estado_0, Coluna_1[0], Coluna_1[1], ~Linha_1[0], ~Linha_1[1]);  // AND_Gate
  Counter #(.width(1), .max('h1)) counter_20 (
    .Q(saida0011), .clk(ACERTADO_0011), .clr(Reset));  // open: load, D, count, carry
  and and_99 (and_99_out, Estado_2, Coluna_2[0], Coluna_2[1], Linha_2[0], ~Linha_2[1]);  // AND_Gate
  and and_100 (and_100_out, ~Estado_0, Coluna_1[0], Coluna_1[1], Linha_1[0], ~Linha_1[1]);  // AND_Gate
  Counter #(.width(1), .max('h1)) counter_21 (
    .Q(saida0111), .clk(ACERTADO_0111), .clr(Reset));  // open: load, D, count, carry
  Counter #(.width(1), .max('h1)) counter_22 (
    .Q(saida1011), .clk(ACERTADO_1011), .clr(Reset));  // open: load, D, count, carry
  Counter #(.width(1), .max('h1)) counter_23 (
    .Q(saida1111), .clk(ACERTADO_1111), .clr(Reset));  // open: load, D, count, carry
  or or_30 (MUX_0011, and_97_out, and_98_out, saida0011);
  or or_31 (MUX_0111, and_99_out, and_100_out, saida0111);
  and and_101 (and_101_out, Estado_2, Coluna_2[0], Coluna_2[1], ~Linha_2[0], Linha_2[1]);  // AND_Gate
  and and_102 (and_102_out, ~Estado_0, Coluna_1[0], Coluna_1[1], ~Linha_1[0], Linha_1[1]);  // AND_Gate
  and and_103 (and_103_out, Estado_2, Coluna_2[0], Coluna_2[1], Linha_2[0], Linha_2[1]);
  and and_104 (and_104_out, ~Estado_0, Coluna_1[0], Coluna_1[1], Linha_1[0], Linha_1[1]);  // AND_Gate
  or or_32 (MUX_1011, and_101_out, and_102_out, saida1011);
  or or_33 (MUX_1111, and_103_out, and_104_out, saida1111);
  and and_105 (and_105_out, ~saida0000, ~Linha[0], ~Linha[1], ~Coluna[0], ~Coluna[1]);  // AND_Gate
  and and_106 (and_106_out, ~saida0100, Linha[0], ~Linha[1], ~Coluna[0], ~Coluna[1]);  // AND_Gate
  and and_107 (and_107_out, ~saida1000, ~Linha[0], Linha[1], ~Coluna[0], ~Coluna[1]);  // AND_Gate
  and and_108 (and_108_out, ~saida1100, Linha[0], Linha[1], ~Coluna[0], ~Coluna[1]);  // AND_Gate
  // NOT_Gate not_1 is placed but not wired
  and and_109 (and_109_out, ~saida0001, ~Linha[0], ~Linha[1], Coluna[0], ~Coluna[1]);  // AND_Gate
  and and_110 (and_110_out, ~saida0101, Linha[0], ~Linha[1], Coluna[0], ~Coluna[1]);  // AND_Gate
  and and_111 (and_111_out, ~saida1001, ~Linha[0], Linha[1], Coluna[0], ~Coluna[1]);  // AND_Gate
  and and_112 (and_112_out, ~saida1101, Linha[0], Linha[1], Coluna[0], ~Coluna[1]);  // AND_Gate
  or or_34 (NAO_ACERTADO, and_108_out, and_107_out, and_106_out, and_105_out, and_112_out, and_111_out, and_110_out, and_109_out, and_116_out, and_115_out, and_114_out, and_113_out, and_120_out, and_119_out, and_118_out, and_117_out);
  and and_113 (and_113_out, ~saida0010, ~Linha[0], ~Linha[1], ~Coluna[0], Coluna[1]);  // AND_Gate
  and and_114 (and_114_out, ~saida0110, Linha[0], ~Linha[1], ~Coluna[0], Coluna[1]);  // AND_Gate
  and and_115 (and_115_out, ~saida1010, ~Linha[0], Linha[1], ~Coluna[0], Coluna[1]);  // AND_Gate
  and and_116 (and_116_out, ~saida1110, Linha[0], Linha[1], ~Coluna[0], Coluna[1]);  // AND_Gate
  and and_117 (and_117_out, ~saida0011, ~Linha[0], ~Linha[1], Coluna[0], Coluna[1]);  // AND_Gate
  and and_118 (and_118_out, ~saida0111, Linha[0], ~Linha[1], Coluna[0], Coluna[1]);  // AND_Gate
  and and_119 (and_119_out, ~saida1011, ~Linha[0], Linha[1], Coluna[0], Coluna[1]);  // AND_Gate
  and and_120 (and_120_out, ~saida1111, Linha[0], Linha[1], Coluna[0], Coluna[1]);  // AND_Gate

  // Notes on the sheet:
  //   MATCHING GAME
endmodule

module escolher (
  input  a,
  input  b,
  output s1,
  output s2
);

  wire not_1_out;

  not not_1 (not_1_out, a);
  and and_1 (s2, a, b);
  and and_2 (s1, not_1_out, b);
endmodule

module iguais (
  input  conf,
  input  comp,
  input  est1,
  output s
);

  wire and_1_out, and_2_out, not_1_out, not_2_out;

  not not_1 (not_1_out, comp);
  not not_2 (not_2_out, est1);
  and and_1 (and_1_out, conf, not_1_out);
  and and_2 (and_2_out, conf, not_2_out);
  or or_1 (s, and_1_out, and_2_out);
endmodule

module jogador_da_vez (
  input  a,
  input  b,
  input  c,
  input  d,
  output x1,
  output x2,
  output x3,
  output x4
);

  wire not_1_out, not_2_out, not_3_out, not_4_out, not_5_out, not_6_out, not_7_out;

  not not_1 (not_1_out, a);
  not not_2 (not_2_out, b);
  not not_3 (not_3_out, c);
  not not_4 (not_4_out, a);
  not not_5 (not_5_out, b);
  not not_6 (not_6_out, c);
  not not_7 (not_7_out, d);
  and and_1 (x3, not_1_out, not_2_out, not_3_out, d);
  and and_2 (x4, not_4_out, not_5_out, not_6_out, not_7_out);

  assign x1 = 1'b0;
  assign x2 = 1'b0;
endmodule
